# Fritzing sketch Schema en bedrading (saved by Fritzing 0.9.3b)

parts:
  Onderdeel1 = Arduino Uno (Rev3)
  Onderdeel2 = EasyDriver_v44
  M1 = Stepper Motor - Bipolar
  Onderdeel3 = Adafruit TSL2561 [part_number="Adafruit #439"]
  Power_plug1 = Power plug

nets:
  N1: Onderdeel1.A4/SDA, Onderdeel3.SDA
  N2: Onderdeel1.A5/SCL, Onderdeel3.SCL
  N3: Onderdeel1.D3_PWM, Onderdeel2.STEP
  N4: Onderdeel1.D4, Onderdeel2.ENABLE
  N5: Onderdeel1.D5_PWM, Onderdeel2.DIR
  5V: Onderdeel1.5V, Onderdeel3.VIN
  GND: Onderdeel1.GND, Onderdeel2.GND, Onderdeel2.MS1, Onderdeel2.SLEEP, Onderdeel2.MS2, Onderdeel2.PFD, Onderdeel2.RESET, Onderdeel3.GND, Power_plug1.GND
  N6: Onderdeel2.V+, Power_plug1.VCC
  N7: Onderdeel2.OUT2A, M1.A
  N8: Onderdeel2.OUT2B, M1.C
  N9: Onderdeel2.OUT1A, M1.B
  N10: Onderdeel2.OUT1B, M1.D

notes:
  TSL2561 Sensor
  6 volt d.m.v. regelaar
  Stappenmotor
  Driver voor de motor
  Arduino UNO
  USB naar PC

custom parts:
  Adafruit TSL2561: The TSL2561 luminosity sensor is an advanced digital light sensor, ideal for use in a wide range of light situations. Compared to low cost CdS cells, this sensor is more precise, allowing for exact lux calculations and can be configured for different gain/timing ranges to detect light ranges from up to 0.1 - 40,000+ Lux on the fly. The best part of this sensor is that it contains both infrared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
